// Logisim project ComplementoDois.circ as structural Verilog: 1 circuit, main circuit ComplementoDois
module ComplementoDois (
  input  A0,
  input  B0,
  input  C0,
  input  D0,
  output A1,
  output B1,
  output C1,
  output D1
);

  wire and_1_out, and_2_out, and_3_out, and_4_out, and_5_out, and_6_out, and_7_out, and_8_out, and_9_out,
       not_1_out, not_2_out, not_3_out, not_4_out, not_5_out, not_6_out, not_7_out, not_8_out, not_9_out,
       not_10_out, not_11_out, not_12_out;

  not not_1 (not_1_out, A0);
  not not_2 (not_2_out, A0);
  not not_3 (not_3_out, A0);
  not not_4 (not_4_out, B0);
  not not_5 (not_5_out, C0);
  not not_6 (not_6_out, D0);
  not not_7 (not_7_out, B0);
  and and_1 (and_1_out, not_7_out, D0);
  not not_8 (not_8_out, B0);
  and and_2 (and_2_out, not_8_out, C0);
  and and_3 (and_3_out, B0, not_9_out, not_10_out);
  not not_9 (not_9_out, C0);
  not not_10 (not_10_out, D0);
  not not_11 (not_11_out, C0);
  and and_4 (and_4_out, not_11_out, D0);
  and and_5 (and_5_out, C0, not_12_out);
  not not_12 (not_12_out, D0);
  and and_6 (and_6_out, not_1_out, D0);
  and and_7 (and_7_out, not_2_out, C0);
  and and_8 (and_8_out, not_3_out, B0);
  and and_9 (and_9_out, A0, not_4_out, not_5_out, not_6_out);
  or or_1 (B1, and_1_out, and_2_out, and_3_out);
  or or_2 (C1, and_4_out, and_5_out);
  or or_3 (A1, and_6_out, and_7_out, and_8_out, and_9_out);

  assign D1 = D0;
endmodule
