// Logisim project Representação C2.circ as structural Verilog: 1 circuit, main circuit main
module main (
  input  A0,
  input  B0,
  input  C0,
  input  D0
);

  wire complementodois_1_a1, complementodois_1_b1, complementodois_1_c1, complementodois_1_d1, demux_21_1_s0,
       demux_21_1_s1, demux_21_2_s0, demux_21_2_s1, demux_21_3_s0, demux_21_3_s1, demux_21_4_s0,
       demux_21_4_s1, hexadecimal_1_a_2, hexadecimal_1_b_2, hexadecimal_1_c_2, hexadecimal_1_d_2,
       hexadecimal_1_e, hexadecimal_1_f, hexadecimal_1_g, or_1_out, or_2_out, or_3_out, or_4_out;

  Demux_21 demux_21_1 (.E(A0), .A(A0), .S0(demux_21_1_s0), .S1(demux_21_1_s1));
  Demux_21 demux_21_2 (.E(B0), .A(A0), .S0(demux_21_2_s0), .S1(demux_21_2_s1));
  Demux_21 demux_21_3 (.E(C0), .A(A0), .S0(demux_21_3_s0), .S1(demux_21_3_s1));
  Demux_21 demux_21_4 (.E(D0), .A(A0), .S0(demux_21_4_s0), .S1(demux_21_4_s1));
  or or_1 (or_1_out, demux_21_1_s0, complementodois_1_a1);
  or or_2 (or_2_out, demux_21_2_s0, complementodois_1_b1);
  ComplementoDois complementodois_1 (
    .A0(demux_21_1_s1), .B0(demux_21_2_s1), .C0(demux_21_3_s1), .D0(demux_21_4_s1),
    .A1(complementodois_1_a1), .B1(complementodois_1_b1), .C1(complementodois_1_c1), .D1(complementodois_1_d1));
  or or_3 (or_3_out, demux_21_3_s0, complementodois_1_c1);
  or or_4 (or_4_out, demux_21_4_s0, complementodois_1_d1);
  Hexadecimal hexadecimal_1 (
    .A(or_1_out), .B(or_2_out), .C(or_3_out), .D(or_4_out), .a_2(hexadecimal_1_a_2), .b_2(hexadecimal_1_b_2),
    .c_2(hexadecimal_1_c_2), .d_2(hexadecimal_1_d_2), .e(hexadecimal_1_e), .f(hexadecimal_1_f),
    .g(hexadecimal_1_g));
  _7_Segment_Display u_7_segment_display_1 (.g(A0));  // open: f, a, b, e, d, c, dp
  _7_Segment_Display u_7_segment_display_2 (
    .g(hexadecimal_1_g), .f(hexadecimal_1_f), .a(hexadecimal_1_a_2), .b(hexadecimal_1_b_2),
    .e(hexadecimal_1_e), .d(hexadecimal_1_d_2), .c(hexadecimal_1_c_2));  // open: dp
endmodule
