// Logisim project PROJETO - SomadorSubtrador C2.circ as structural Verilog: 1 circuit, main circuit main
module main (
  input  A0,
  input  B0,
  input  C0,
  input  D0,
  input  A1,
  input  B1,
  input  C1,
  input  D1
);

  wire and_1_out, hexadecimal_1_a_2, hexadecimal_1_b_2, hexadecimal_1_c_2, hexadecimal_1_d_2,
       hexadecimal_1_e, hexadecimal_1_f, hexadecimal_1_g, main_1_s0, main_1_s1, main_1_s2, main_1_s3,
       main_2_a1, main_2_b1, main_2_c1, main_2_d1, or_1_out, xor_1_out;

  and and_1 (and_1_out, A1, A0);
  xor xor_1 (xor_1_out, A1, A0);
  Somador_C2___4_Bits_main main_1 (
    .A3(A0), .A2(B0), .A1(C0), .A0(D0), .B3(A1), .B2(B1), .B1(C1), .B0(D1), .S0(main_1_s0), .S1(main_1_s1),
    .S2(main_1_s2), .S3(main_1_s3));
  \Representação_C2___SomadorSubtrador_main  main_2 (
    .A0(main_1_s3), .B0(main_1_s2), .C0(main_1_s1), .D0(main_1_s0), .A1(main_2_a1), .B1(main_2_b1),
    .C1(main_2_c1), .D1(main_2_d1));
  or or_1 (or_1_out, and_1_out, xor_1_out);
  Hexadecimal hexadecimal_1 (
    .A(main_2_a1), .B(main_2_b1), .C(main_2_c1), .D(main_2_d1), .a_2(hexadecimal_1_a_2),
    .b_2(hexadecimal_1_b_2), .c_2(hexadecimal_1_c_2), .d_2(hexadecimal_1_d_2), .e(hexadecimal_1_e),
    .f(hexadecimal_1_f), .g(hexadecimal_1_g));
  _7_Segment_Display u_7_segment_display_1 (.g(or_1_out));  // open: f, a, b, e, d, c, dp
  _7_Segment_Display u_7_segment_display_2 (
    .g(hexadecimal_1_g), .f(hexadecimal_1_f), .a(hexadecimal_1_a_2), .b(hexadecimal_1_b_2),
    .e(hexadecimal_1_e), .d(hexadecimal_1_d_2), .c(hexadecimal_1_c_2));  // open: dp
endmodule
