// Logisim project Biblioteca - Somador01.circ as structural Verilog: 1 circuit, main circuit main
module main (
  input  B3,
  input  A3,
  input  B2,
  input  A2,
  input  B1,
  input  A1,
  input  B0,
  input  A0,
  output S3,
  output S2,
  output S1,
  output S0
);

  wire somador_1_p1, somador_2_p1, somador_3_p3;

  // Somador somador_1: pin names not known; wires that end beside it: somador_1_p1, B3, A3, S3
  // Somador somador_2: pin names not known; wires that end beside it: somador_2_p1, B2, somador_1_p1, A2, S2
  // Somador somador_3: pin names not known; wires that end beside it: 1'b0, B0, somador_3_p3, A0, S0
  // Somador somador_4: pin names not known; wires that end beside it: somador_3_p3, B1, somador_2_p1, A1, S1
endmodule
