// Logisim project Pré - Somador e Subtrador.circ as structural Verilog: 1 circuit, main circuit SomadorSubtrador
module SomadorSubtrador (
  input  M,
  input  A,
  input  B,
  input  Cin,
  output S,
  output Cout
);

  wire and_1_out, and_2_out, and_3_out, and_4_out, and_5_out, and_6_out, and_7_out, and_8_out, and_9_out,
       not_1_out, not_2_out, not_3_out, not_4_out, not_5_out, not_6_out, not_7_out, not_8_out, not_9_out,
       not_10_out;

  not not_1 (not_1_out, A);
  and and_1 (and_1_out, not_1_out, not_2_out, Cin);
  not not_2 (not_2_out, B);
  not not_3 (not_3_out, A);
  and and_2 (and_2_out, not_3_out, B, not_4_out);
  not not_4 (not_4_out, Cin);
  not not_5 (not_5_out, B);
  and and_3 (and_3_out, A, not_5_out, not_6_out);
  not not_6 (not_6_out, Cin);
  and and_4 (and_4_out, A, B, Cin);
  and and_5 (and_5_out, B, Cin);
  not not_7 (not_7_out, M);
  and and_6 (and_6_out, not_7_out, A, Cin);
  not not_8 (not_8_out, M);
  and and_7 (and_7_out, not_8_out, A, B);
  not not_9 (not_9_out, A);
  and and_8 (and_8_out, M, not_9_out, Cin);
  and and_9 (and_9_out, M, not_10_out, B);
  not not_10 (not_10_out, A);
  or or_1 (S, and_1_out, and_2_out, and_3_out, and_4_out);
  or or_2 (Cout, and_5_out, and_6_out, and_7_out, and_8_out, and_9_out);
endmodule
