// Logisim project Somador e Subtrador.circ as structural Verilog: 1 circuit, main circuit main
module main (
  input  \Troca_operação ,
  input  A1,
  input  B1,
  input  C1,
  input  D1,
  input  A2,
  input  B2,
  input  C2,
  input  C2_2
);

  wire hexadecimal_1_a_2, hexadecimal_1_b_2, hexadecimal_1_c_2, hexadecimal_1_d_2, hexadecimal_1_e,
       hexadecimal_1_f, hexadecimal_1_g, Q0_cout, Q0_s, Q1_cout, Q1_s, Q2_cout, Q2_s, Q3_s;

  SomadorSubtrador Q3 (.M(\Troca_operação ), .A(A1), .B(A2), .Cin(Q2_cout), .S(Q3_s));  // open: Cout
  SomadorSubtrador Q2 (.M(\Troca_operação ), .A(B1), .B(B2), .Cin(Q1_cout), .S(Q2_s), .Cout(Q2_cout));
  SomadorSubtrador Q1 (.M(\Troca_operação ), .A(C1), .B(C2), .Cin(Q0_cout), .S(Q1_s), .Cout(Q1_cout));
  SomadorSubtrador Q0 (.M(\Troca_operação ), .A(D1), .B(C2_2), .Cin(1'b0), .S(Q0_s), .Cout(Q0_cout));
  Hexadecimal hexadecimal_1 (
    .A(Q3_s), .B(Q2_s), .C(Q1_s), .D(Q0_s), .a_2(hexadecimal_1_a_2), .b_2(hexadecimal_1_b_2),
    .c_2(hexadecimal_1_c_2), .d_2(hexadecimal_1_d_2), .e(hexadecimal_1_e), .f(hexadecimal_1_f),
    .g(hexadecimal_1_g));
  _7_Segment_Display u_7_segment_display_1 (
    .g(hexadecimal_1_g), .f(hexadecimal_1_f), .a(hexadecimal_1_a_2), .b(hexadecimal_1_b_2),
    .e(hexadecimal_1_e), .d(hexadecimal_1_d_2), .c(hexadecimal_1_c_2));  // open: dp

  // Notes on the sheet:
  //   0 - Soma
  //   1 - Subtração
endmodule
