// Logisim project Biblioteca - Subtrador01.circ as structural Verilog: 1 circuit, main circuit main
module main (
  input  A3,
  input  B3,
  input  A2,
  input  B2,
  input  A1,
  input  B1,
  input  A0,
  input  B0,
  output S3,
  output S2,
  output S1,
  output S0
);

  wire subtrador_2_cout, subtrador_3_cout, subtrador_4_cout;

  Subtrador subtrador_1 (.A(A3), .B(B3), .Cin(subtrador_2_cout), .S(S3));  // open: Cout
  Subtrador subtrador_2 (.A(A2), .B(B2), .Cin(subtrador_3_cout), .S(S2), .Cout(subtrador_2_cout));
  Subtrador subtrador_3 (.A(A1), .B(B1), .Cin(subtrador_4_cout), .S(S1), .Cout(subtrador_3_cout));
  Subtrador subtrador_4 (.A(A0), .B(B0), .Cin(1'b0), .S(S0), .Cout(subtrador_4_cout));
endmodule
