// Logisim project Subtrador.circ as structural Verilog: 1 circuit, main circuit main
module main (
  input  A3,
  input  A2,
  input  A1,
  input  A0,
  input  B3,
  input  B2,
  input  B1,
  input  B0
);

  wire hexadecimal_1_a_2, hexadecimal_1_b_2, hexadecimal_1_c_2, hexadecimal_1_d_2, hexadecimal_1_e,
       hexadecimal_1_f, hexadecimal_1_g, main_1_s0, main_1_s1, main_1_s2, main_1_s3;

  Hexadecimal hexadecimal_1 (
    .A(main_1_s3), .B(main_1_s2), .C(main_1_s1), .D(main_1_s0), .a_2(hexadecimal_1_a_2),
    .b_2(hexadecimal_1_b_2), .c_2(hexadecimal_1_c_2), .d_2(hexadecimal_1_d_2), .e(hexadecimal_1_e),
    .f(hexadecimal_1_f), .g(hexadecimal_1_g));
  Biblioteca___Subtrador01_main main_1 (
    .S3(main_1_s3), .S2(main_1_s2), .S1(main_1_s1), .S0(main_1_s0), .A3(A3), .B3(B3), .A2(A2), .B2(B2),
    .A1(A1), .B1(B1), .A0(A0), .B0(B0));
  _7_Segment_Display u_7_segment_display_1 (
    .g(hexadecimal_1_g), .f(hexadecimal_1_f), .a(hexadecimal_1_a_2), .b(hexadecimal_1_b_2),
    .e(hexadecimal_1_e), .d(hexadecimal_1_d_2), .c(hexadecimal_1_c_2));  // open: dp
endmodule
