// Logisim project CodificadorDecodificador.circ as structural Verilog: 1 circuit, main circuit main
module main (
);

  wire _0_out, _1_out, _2_out, _3_out, _4_out, _5_out, _6_out, _7_out, _8_out, _9_out, codificador_1_a_2,
       codificador_1_b_2, codificador_1_c_2, codificador_1_d_2, decodificador09_1_p5, decodificador09_1_p6,
       decodificador09_1_p7, decodificador09_1_p8, decodificador09_1_p9, decodificador09_1_p10,
       decodificador09_1_p11;

  Button _2 (.out(_2_out));
  Button _1 (.out(_1_out));
  Button _4 (.out(_4_out));
  Button _5 (.out(_5_out));
  Button _7 (.out(_7_out));
  Button _8 (.out(_8_out));
  Button _0 (.out(_0_out));
  Button _3 (.out(_3_out));
  Button _6 (.out(_6_out));
  Button _9 (.out(_9_out));
  Codificador codificador_1 (
    .a(_1_out), .b(_2_out), .c(_3_out), .d(_4_out), .e(_5_out), .f(_6_out), .g(_7_out), .h(_8_out),
    .i(_9_out), .j(_0_out), .a_2(codificador_1_a_2), .b_2(codificador_1_b_2), .c_2(codificador_1_c_2),
    .d_2(codificador_1_d_2));
  // Decodificador09 decodificador09_1: pin names not known; wires that end beside it: codificador_1_a_2, codificador_1_b_2, codificador_1_c_2, codificador_1_d_2, decodificador09_1_p5, decodificador09_1_p6, decodificador09_1_p7, decodificador09_1_p8, decodificador09_1_p9, decodificador09_1_p10, decodificador09_1_p11
  _7_Segment_Display u_7_segment_display_1 (
    .g(decodificador09_1_p11), .f(decodificador09_1_p10), .a(decodificador09_1_p5), .b(decodificador09_1_p6),
    .e(decodificador09_1_p9), .d(decodificador09_1_p8), .c(decodificador09_1_p7));  // open: dp
endmodule
