// Logisim project Pré-contador - 99 até 0.circ as structural Verilog: 1 circuit, main circuit main
module main (
  input  Clock,
  output Q3,
  output Q2,
  output Q1,
  output Q0
);

  wire and_1_out, and_2_out, decinall_1_a_2, decinall_1_b_2, decinall_1_c_2, decinall_1_d_2, decinall_1_e,
       decinall_1_f, decinall_1_g, nor_1_out, nor_2_out, or_1_out, Q0_qn;

  J_K_Flip_Flop u_Q3 (.J(nor_2_out), .clk(Clock), .K(Q0_qn), .Q(Q3));  // open: Qn, preset, en, reset
  nor nor_1 (nor_1_out, Q1, Q0);
  J_K_Flip_Flop u_Q2 (.J(and_1_out), .clk(Clock), .K(nor_1_out), .Q(Q2));  // open: Qn, preset, en, reset
  and and_1 (and_1_out, Q3, Q0_qn);
  or or_1 (or_1_out, Q3, Q2);
  and and_2 (and_2_out, or_1_out, Q0_qn);
  J_K_Flip_Flop u_Q1 (.J(and_2_out), .clk(Clock), .K(Q0_qn), .Q(Q1));  // open: Qn, preset, en, reset
  J_K_Flip_Flop u_Q0 (.J(1'b1), .clk(Clock), .K(1'b1), .Q(Q0), .Qn(Q0_qn));  // open: preset, en, reset
  nor nor_2 (nor_2_out, Q0, Q1, Q2);
  Decinall decinall_1 (
    .A(Q3), .B(Q2), .a_2(decinall_1_a_2), .C(Q1), .D(Q0), .b_2(decinall_1_b_2), .c_2(decinall_1_c_2),
    .d_2(decinall_1_d_2), .e(decinall_1_e), .f(decinall_1_f), .g(decinall_1_g));
  _7_Segment_Display u_7_segment_display_1 (
    .g(decinall_1_g), .f(decinall_1_f), .a(decinall_1_a_2), .b(decinall_1_b_2), .e(decinall_1_e),
    .d(decinall_1_d_2), .c(decinall_1_c_2));  // open: dp
endmodule
